# Fritzing sketch button controler (saved by Fritzing 0.9.1b)
breadboards: 1

parts:
  Composant1 = Arduino Uno (Rev3)
  S1 = Pushbutton [package="[THT]"]
  S2 = Pushbutton [package="[THT]"]
  S3 = Pushbutton [package="[THT]"]
  S4 = Pushbutton [package="[THT]"]
  S5 = Pushbutton [package="[THT]"]
  R1 = Resistor [tolerance=±5% resistance=1k package=THT]
  R2 = Resistor [tolerance=±5% resistance=1k package=THT]
  R3 = Resistor [tolerance=±5% resistance=1k package=THT]
  R4 = Resistor [tolerance=±5% resistance=1k package=THT]
  R5 = Resistor [tolerance=±5% resistance=1k package=THT]

nets:
  N1: Composant1.D2, S1.Pin_1, S1.Pin_2, R1.Pin_0
  N2: Composant1.D3_PWM, S2.Pin_1, S2.Pin_2, R2.Pin_0
  N3: Composant1.D4, S3.Pin_1, S3.Pin_2, R3.Pin_0
  N4: Composant1.D5_PWM, S4.Pin_1, S4.Pin_2, R4.Pin_0
  N5: Composant1.D6_PWM, S5.Pin_1, S5.Pin_2, R5.Pin_0
  N6: Composant1.5V, S1.Pin_3, S1.Pin_4, S2.Pin_3, S2.Pin_4, S3.Pin_3, S3.Pin_4, S4.Pin_3, S4.Pin_4, S5.Pin_3, S5.Pin_4
  N7: Composant1.GND, R1.Pin_1, R2.Pin_1, R3.Pin_1, R4.Pin_1, R5.Pin_1

// code stored in the sketch: Untitled.ino
// 
// 3 button circuit
// 
// Made by Valentin Hayot
// License: CC-BY-SA 3.0
// Downloaded from: http://123d.circuits.io/circuits/559218-the-unnamed-circuit

// Pin 13 has an LED connected on most Arduino boards.
// give it a name:
int led = 13;

const int buttonPin1 = 2;
const int buttonPin2 = 3;
const int buttonPin3 = 4;
const int buttonPin4 = 5;
const int buttonPin5 = 6;
int lastval = 0;

// the setup routine runs once when you press reset:
void setup() {
  // initialize the digital pin as an output.
  Serial.begin(9600);
  pinMode(led, OUTPUT);
  pinMode(buttonPin1, INPUT);
  pinMode(buttonPin2, INPUT);
  pinMode(buttonPin3, INPUT);
  pinMode(buttonPin4, INPUT);
  pinMode(buttonPin5, INPUT);
  Serial.println("yop");
  
}

// the loop routine runs over and over again forever:
void loop() {
  if(digitalRead(buttonPin1) == HIGH )
  {
    if(lastval != buttonPin1)
     Serial.println("1");
     digitalWrite(led, HIGH);
  	lastval = buttonPin1;
  }
  else if(digitalRead(buttonPin2) == HIGH)
  {
    if(lastval != buttonPin2)
   	 Serial.println("2");
     digitalWrite(led, HIGH);
    lastval = buttonPin2;
  }
  else if(digitalRead(buttonPin3) == HIGH)
  {
    if(lastval != buttonPin3)
     Serial.println("3");
     digitalWrite(led, HIGH);
    lastval = buttonPin3;
  }
  else if(digitalRead(buttonPin4) == HIGH)
  {
    if(lastval != buttonPin4)
     Serial.println("4");
     digitalWrite(led, HIGH);
    lastval = buttonPin4;
  }
  else if(digitalRead(buttonPin5) == HIGH)
  {
    if(lastval != buttonPin5)
     Serial.println("5");
     digitalWrite(led, HIGH);
 	lastval = buttonPin5;
  }
  else
  {
    if(lastval != 0)
      Serial.println("0");   
    digitalWrite(led, LOW);   
  	lastval = 0;
  }
  
  

}
